# Fritzing sketch ledBoard2 (saved by Fritzing 0.9.2b)
circuit board: 7.03423cm x 6.23049cm
breadboards: 1

parts:
  0 = LED - 5mm [color="Red (633nm)" package="5 mm [THT]"]
  2 = LED - 5mm [color="Red (633nm)" package="5 mm [THT]"]
  1 = LED - 5mm [color="Red (633nm)" package="5 mm [THT]"]
  4 = LED - 5mm [color="Red (633nm)" package="5 mm [THT]"]
  3 = LED - 5mm [color="Red (633nm)" package="5 mm [THT]"]
  5 = LED - 5mm [color="Red (633nm)" package="5 mm [THT]"]
  7 = LED - 5mm [color="Red (633nm)" package="5 mm [THT]"]
  8 = LED - 5mm [color="Red (633nm)" package="5 mm [THT]"]
  9 = LED - 5mm [color="Red (633nm)" package="5 mm [THT]"]
  6 = LED - 5mm [color="Red (633nm)" package="5 mm [THT]"]
  13 = LED - 5mm [color="Red (633nm)" package="5 mm [THT]"]
  14 = LED - 5mm [color="Red (633nm)" package="5 mm [THT]"]
  12 = LED - 5mm [color="Red (633nm)" package="5 mm [THT]"]
  11 = LED - 5mm [color="Red (633nm)" package="5 mm [THT]"]
  10 = LED - 5mm [color="Red (633nm)" package="5 mm [THT]"]
  15 = LED - 5mm [color="Red (633nm)" package="5 mm [THT]"]
  16 = LED - 5mm [color="Red (633nm)" package="5 mm [THT]"]
  17 = LED - 5mm [color="Red (633nm)" package="5 mm [THT]"]
  18 = LED - 5mm [color="Red (633nm)" package="5 mm [THT]"]
  19 = LED - 5mm [color="Red (633nm)" package="5 mm [THT]"]
  20 = LED - 5mm [color="Red (633nm)" package="5 mm [THT]"]
  21 = LED - 5mm [color="Red (633nm)" package="5 mm [THT]"]
  22 = LED - 5mm [color="Red (633nm)" package="5 mm [THT]"]
  23 = LED - 5mm [color="Red (633nm)" package="5 mm [THT]"]
  24 = LED - 5mm [color="Red (633nm)" package="5 mm [THT]"]
  part = Header 12 [package=1x12_machine-pin-header_lock.004]

nets:
  N1: 0.cathode, 2.cathode, 1.cathode, 4.cathode, 3.cathode, part.5
  N2: 0.anode, 5.anode, 10.anode, 15.anode, 20.anode, part.12
  N3: 2.anode, 7.anode, 12.anode, 17.anode, 22.anode, part.10
  N4: 1.anode, 6.anode, 11.anode, 16.anode, 21.anode, part.11
  N5: 4.anode, 9.anode, 14.anode, 19.anode, 24.anode, part.8
  N6: 3.anode, 8.anode, 13.anode, 18.anode, 23.anode, part.9
  N7: 5.cathode, 7.cathode, 8.cathode, 9.cathode, 6.cathode, part.4
  N8: 13.cathode, 14.cathode, 12.cathode, 11.cathode, 10.cathode, part.3
  N9: 15.cathode, 16.cathode, 17.cathode, 18.cathode, 19.cathode, part.2
  N10: 20.cathode, 21.cathode, 22.cathode, 23.cathode, 24.cathode, part.1

notes:
  informatik.uibk.ac.at
  4 3 2 1 0
  Cathodes
  Anodes
